// Logisim project And.circ as structural Verilog: 1 circuit, main circuit main
module main (
  input  A,
  input  B,
  output O
);

  wire nand_1_out;

  nand nand_1 (nand_1_out, A, B);
  nand nand_2 (O, nand_1_out, nand_1_out);
endmodule
