// Logisim project And16.circ as structural Verilog: 1 circuit, main circuit main
module main (
  input  [15:0] A,
  input  [15:0] B,
  output [15:0] O
);

  assign O = A & B;  // AND_Gate and_1, 16 bits wide
endmodule
