// Logisim project DMux.circ as structural Verilog: 1 circuit, main circuit main
module main (
  input  I,
  input  Sel,
  output A,
  output B
);

  wire not_1_out;

  not not_1 (not_1_out, Sel);
  and and_1 (A, I, not_1_out);
  and and_2 (B, Sel, I);
endmodule
