// Logisim project DMux8Way.circ as structural Verilog: 1 circuit, main circuit main
module main (
  input  I,
  input  [2:0] Sel,
  output O0,
  output O1,
  output O2,
  output O3,
  output O4,
  output O5,
  output O6,
  output O7
);

  Demultiplexer #(.select(3)) demultiplexer_1 (
    .out0(O0), .out1(O1), .out2(O2), .out3(O3), .out4(O4), .out5(O5), .out6(O6), .out7(O7), .in(I), .sel(Sel));
endmodule
