// Logisim project Dmux4Way.circ as structural Verilog: 1 circuit, main circuit main
module main (
  input  I,
  input  [1:0] Sel,
  output O0,
  output O1,
  output O2,
  output O3
);

  Demultiplexer #(.select(2)) demultiplexer_1 (.out0(O0), .out1(O1), .out2(O2), .out3(O3), .in(I), .sel(Sel));
endmodule
