// Logisim project Mux.circ as structural Verilog: 1 circuit, main circuit main
module main (
  input  A,
  input  Sel,
  input  B,
  output O
);

  wire and_1_out, and_2_out, not_1_out;

  not not_1 (not_1_out, Sel);
  and and_1 (and_1_out, A, not_1_out);
  and and_2 (and_2_out, B, Sel);
  or or_1 (O, and_1_out, and_2_out);
endmodule
