// Logisim project Mux16.circ as structural Verilog: 1 circuit, main circuit main
module main (
  input  [15:0] A,
  input  [15:0] B,
  input  Sel,
  output [15:0] O
);

  Multiplexer #(.width(16)) multiplexer_1 (.in0(A), .in1(B), .out(O), .sel(Sel));
endmodule
