// Logisim project Mux4Way16.circ as structural Verilog: 1 circuit, main circuit main
module main (
  input  [15:0] A,
  input  [15:0] B,
  input  [15:0] C,
  input  Sel2,
  input  [15:0] D,
  input  Sel1,
  output [15:0] O
);

  wire [15:0] multiplexer_1_out, multiplexer_2_out;

  Multiplexer #(.width(16)) multiplexer_1 (.in0(A), .in1(B), .out(multiplexer_1_out), .sel(Sel1));
  Multiplexer #(.width(16)) multiplexer_2 (.in0(C), .in1(D), .out(multiplexer_2_out), .sel(Sel1));
  Multiplexer #(.width(16)) multiplexer_3 (.in0(multiplexer_1_out), .in1(multiplexer_2_out), .out(O), .sel(Sel2));
endmodule
