// Logisim project Mux8Way16.circ as structural Verilog: 1 circuit, main circuit main
module main (
  input  [15:0] A,
  input  [15:0] B,
  input  [15:0] C,
  input  [15:0] D,
  input  [15:0] E,
  input  Sel3,
  input  [15:0] F,
  input  [15:0] G,
  input  Sel2,
  input  [15:0] H,
  input  Sel1,
  output [15:0] out_12
);

  wire [15:0] multiplexer_1_out, multiplexer_2_out, multiplexer_3_out, multiplexer_4_out, multiplexer_5_out,
       multiplexer_6_out;

  Multiplexer #(.width(16)) multiplexer_1 (.in0(A), .in1(B), .out(multiplexer_1_out), .sel(Sel1));
  Multiplexer #(.width(16)) multiplexer_2 (.in0(C), .in1(D), .out(multiplexer_2_out), .sel(Sel1));
  Multiplexer #(.width(16)) multiplexer_3 (.in0(E), .in1(F), .out(multiplexer_3_out), .sel(Sel1));
  Multiplexer #(.width(16)) multiplexer_4 (.in0(G), .in1(H), .out(multiplexer_4_out), .sel(Sel1));
  Multiplexer #(.width(16)) multiplexer_5 (
    .in0(multiplexer_1_out), .in1(multiplexer_2_out), .out(multiplexer_5_out), .sel(Sel2));
  Multiplexer #(.width(16)) multiplexer_6 (
    .in0(multiplexer_3_out), .in1(multiplexer_4_out), .out(multiplexer_6_out), .sel(Sel2));
  Multiplexer #(.width(16)) multiplexer_7 (.in0(multiplexer_5_out), .in1(multiplexer_6_out), .out(out_12), .sel(Sel3));
endmodule
