// Logisim project Not16.circ as structural Verilog: 1 circuit, main circuit main
module main (
  input  [15:0] I,
  output [15:0] O
);

  assign O = ~I;  // NOT_Gate not_1, 16 bits wide
endmodule
