// Logisim project Or.circ as structural Verilog: 1 circuit, main circuit main
module main (
  input  A,
  input  B,
  output O
);

  wire nand_1_out, nand_2_out;

  nand nand_1 (nand_1_out, A, A);
  nand nand_2 (nand_2_out, B, B);
  nand nand_3 (O, nand_1_out, nand_2_out);
endmodule
