// Logisim project Or8Way.circ as structural Verilog: 1 circuit, main circuit main
module main (
  input  [7:0] I,
  output O
);

  or or_1 (O, I[0], I[1], I[2], I[3], I[4], I[5], I[6], I[7]);
endmodule
