// Logisim project Xor.circ as structural Verilog: 1 circuit, main circuit main
module main (
  input  A,
  input  B,
  output O
);

  wire nand_1_out, or_1_out;

  or or_1 (or_1_out, A, B);
  nand nand_1 (nand_1_out, A, B);
  and and_1 (O, or_1_out, nand_1_out);
endmodule
