// Logisim project ALU.circ as structural Verilog: 1 circuit, main circuit main
module main (
  input  zx,
  input  zy,
  input  nx,
  input  ny,
  input  f,
  input  no,
  input  [15:0] x,
  input  [15:0] falsex,
  input  [15:0] y,
  input  [15:0] falsey,
  output [15:0] outM,
  output zr,
  output ng
);

  wire or_1_out, or_2_out, or_3_out;
  wire [15:0] adder_1_out, and_1_out, and_2_out, and_3_out, multiplexer_1_out, multiplexer_2_out,
       multiplexer_3_out, multiplexer_4_out, multiplexer_5_out, not_1_out, not_2_out, not_3_out;

  assign and_1_out = x & falsex;  // AND_Gate and_1, 16 bits wide
  assign and_2_out = y & falsey;  // AND_Gate and_2, 16 bits wide
  Multiplexer #(.width(16)) multiplexer_1 (.in0(x), .in1(and_1_out), .out(multiplexer_1_out), .sel(zx));
  Multiplexer #(.width(16)) multiplexer_2 (.in0(y), .in1(and_2_out), .out(multiplexer_2_out), .sel(zy));
  assign not_1_out = ~multiplexer_1_out;  // NOT_Gate not_1, 16 bits wide
  assign not_2_out = ~multiplexer_2_out;  // NOT_Gate not_2, 16 bits wide
  Multiplexer #(.width(16)) multiplexer_3 (.in0(multiplexer_1_out), .in1(not_1_out), .out(multiplexer_3_out), .sel(nx));
  Multiplexer #(.width(16)) multiplexer_4 (.in0(multiplexer_2_out), .in1(not_2_out), .out(multiplexer_4_out), .sel(ny));
  assign and_3_out = multiplexer_3_out & multiplexer_4_out;  // AND_Gate and_3, 16 bits wide
  Adder #(.width(16)) adder_1 (.a(multiplexer_3_out), .b(multiplexer_4_out), .out(adder_1_out));  // open: cin, cout
  Multiplexer #(.width(16)) multiplexer_5 (.in0(and_3_out), .in1(adder_1_out), .out(multiplexer_5_out), .sel(f));
  assign not_3_out = ~multiplexer_5_out;  // NOT_Gate not_3, 16 bits wide
  Multiplexer #(.width(16)) multiplexer_6 (.in0(multiplexer_5_out), .in1(not_3_out), .out({ng, outM[14:0]}), .sel(no));
  or or_1 (or_1_out, outM[0], outM[1], outM[2], outM[3], outM[4], outM[5], outM[6], outM[7]);
  or or_2 (or_2_out, outM[8], outM[9], outM[10], outM[11], outM[12], outM[13], outM[14], ng);
  or or_3 (or_3_out, or_1_out, or_2_out);
  not not_4 (zr, or_3_out);

  assign outM[15] = ng;
endmodule
