// Logisim project Add16.circ as structural Verilog: 1 circuit, main circuit main
module main (
  input  A0,
  input  A1,
  input  A2,
  input  A3,
  input  A4,
  input  A5,
  input  A6,
  input  A7,
  input  A8,
  input  A9,
  input  A10,
  input  A11,
  input  A12,
  input  A13,
  input  A14,
  input  A15,
  input  B0,
  input  B1,
  input  B2,
  input  B3,
  input  B4,
  input  B5,
  input  B6,
  input  B7,
  input  B8,
  input  B9,
  input  B10,
  input  B11,
  input  B12,
  input  B13,
  input  B14,
  input  B15,
  output overflow,
  output sum0,
  output sum1,
  output sum2,
  output sum3,
  output sum4,
  output sum5,
  output sum6,
  output sum7,
  output sum8,
  output sum9,
  output sum10,
  output sum11,
  output sum12,
  output sum13,
  output sum14,
  output sum15
);

  wire and_1_out, and_2_out, and_3_out, and_4_out, and_5_out, and_6_out, and_7_out, and_8_out, and_9_out,
       and_10_out, and_11_out, and_12_out, and_13_out, and_14_out, and_15_out, and_16_out, and_17_out,
       and_18_out, and_19_out, and_20_out, and_21_out, and_22_out, and_23_out, and_24_out, and_25_out,
       and_26_out, and_27_out, and_28_out, and_29_out, and_30_out, and_31_out, and_32_out, or_1_out,
       or_2_out, or_3_out, or_4_out, or_5_out, or_6_out, or_7_out, or_8_out, or_9_out, or_10_out, or_11_out,
       or_12_out, or_13_out, or_14_out, or_15_out, xor_1_out, xor_3_out, xor_5_out, xor_7_out, xor_9_out,
       xor_11_out, xor_13_out, xor_15_out, xor_17_out, xor_19_out, xor_21_out, xor_23_out, xor_25_out,
       xor_27_out, xor_29_out, xor_31_out;

  and and_1 (and_1_out, B0, A0);
  or or_1 (or_1_out, and_1_out, and_2_out);
  xor xor_1 (xor_1_out, B0, A0);
  and and_2 (and_2_out, xor_1_out, 1'b0);
  xor xor_2 (sum0, xor_1_out, 1'b0);
  and and_3 (and_3_out, B1, A1);
  or or_2 (or_2_out, and_3_out, and_4_out);
  xor xor_3 (xor_3_out, B1, A1);
  xor xor_4 (sum1, xor_3_out, or_1_out);
  and and_4 (and_4_out, xor_3_out, or_1_out);
  and and_5 (and_5_out, B2, A2);
  or or_3 (or_3_out, and_5_out, and_6_out);
  xor xor_5 (xor_5_out, B2, A2);
  and and_6 (and_6_out, xor_5_out, or_2_out);
  xor xor_6 (sum2, xor_5_out, or_2_out);
  and and_7 (and_7_out, B3, A3);
  or or_4 (or_4_out, and_7_out, and_8_out);
  xor xor_7 (xor_7_out, B3, A3);
  and and_8 (and_8_out, xor_7_out, or_3_out);
  xor xor_8 (sum3, xor_7_out, or_3_out);
  and and_9 (and_9_out, B4, A4);
  or or_5 (or_5_out, and_9_out, and_10_out);
  xor xor_9 (xor_9_out, B4, A4);
  and and_10 (and_10_out, xor_9_out, or_4_out);
  xor xor_10 (sum4, xor_9_out, or_4_out);
  and and_11 (and_11_out, B5, A5);
  or or_6 (or_6_out, and_11_out, and_12_out);
  xor xor_11 (xor_11_out, B5, A5);
  and and_12 (and_12_out, xor_11_out, or_5_out);
  xor xor_12 (sum5, xor_11_out, or_5_out);
  and and_13 (and_13_out, B6, A6);
  or or_7 (or_7_out, and_13_out, and_14_out);
  xor xor_13 (xor_13_out, B6, A6);
  and and_14 (and_14_out, xor_13_out, or_6_out);
  xor xor_14 (sum6, xor_13_out, or_6_out);
  and and_15 (and_15_out, B7, A7);
  or or_8 (or_8_out, and_15_out, and_16_out);
  xor xor_15 (xor_15_out, B7, A7);
  and and_16 (and_16_out, xor_15_out, or_7_out);
  xor xor_16 (sum7, xor_15_out, or_7_out);
  and and_17 (and_17_out, B8, A8);
  or or_9 (or_9_out, and_17_out, and_18_out);
  xor xor_17 (xor_17_out, B8, A8);
  and and_18 (and_18_out, xor_17_out, or_8_out);
  xor xor_18 (sum8, xor_17_out, or_8_out);
  and and_19 (and_19_out, B9, A9);
  or or_10 (or_10_out, and_19_out, and_20_out);
  xor xor_19 (xor_19_out, B9, A9);
  and and_20 (and_20_out, xor_19_out, or_9_out);
  xor xor_20 (sum9, xor_19_out, or_9_out);
  and and_21 (and_21_out, B10, A10);
  or or_11 (or_11_out, and_21_out, and_22_out);
  xor xor_21 (xor_21_out, B10, A10);
  and and_22 (and_22_out, xor_21_out, or_10_out);
  xor xor_22 (sum10, xor_21_out, or_10_out);
  and and_23 (and_23_out, B11, A11);
  or or_12 (or_12_out, and_23_out, and_24_out);
  xor xor_23 (xor_23_out, B11, A11);
  xor xor_24 (sum11, xor_23_out, or_11_out);
  and and_24 (and_24_out, xor_23_out, or_11_out);
  and and_25 (and_25_out, B12, A12);
  or or_13 (or_13_out, and_25_out, and_26_out);
  xor xor_25 (xor_25_out, B12, A12);
  and and_26 (and_26_out, xor_25_out, or_12_out);
  xor xor_26 (sum12, xor_25_out, or_12_out);
  and and_27 (and_27_out, B13, A13);
  or or_14 (or_14_out, and_27_out, and_28_out);
  xor xor_27 (xor_27_out, B13, A13);
  and and_28 (and_28_out, xor_27_out, or_13_out);
  xor xor_28 (sum13, xor_27_out, or_13_out);
  and and_29 (and_29_out, B14, A14);
  or or_15 (or_15_out, and_29_out, and_30_out);
  xor xor_29 (xor_29_out, B14, A14);
  and and_30 (and_30_out, xor_29_out, or_14_out);
  xor xor_30 (sum14, xor_29_out, or_14_out);
  and and_31 (and_31_out, B15, A15);
  or or_16 (overflow, and_31_out, and_32_out);
  xor xor_31 (xor_31_out, B15, A15);
  and and_32 (and_32_out, xor_31_out, or_15_out);
  xor xor_32 (sum15, xor_31_out, or_15_out);
endmodule
