// Logisim project Add16_arithmeticUnit.circ as structural Verilog: 1 circuit, main circuit main
module main (
  input  [15:0] A,
  input  [15:0] B,
  output [15:0] O
);

  Adder #(.width(16)) adder_1 (.a(A), .b(B), .out(O));  // open: cin, cout
endmodule
