// Logisim project FullAdder.circ as structural Verilog: 1 circuit, main circuit main
module main (
  input  I,
  input  A,
  input  B,
  output sum,
  output carry
);

  wire and_1_out, and_2_out, xor_1_out;

  xor xor_1 (xor_1_out, A, B);
  and and_1 (and_1_out, B, A);
  xor xor_2 (sum, I, xor_1_out);
  and and_2 (and_2_out, I, xor_1_out);
  or or_1 (carry, and_2_out, and_1_out);
endmodule
