// Logisim project Inc16.circ as structural Verilog: 1 circuit, main circuit main
module main (
  input  [15:0] A,
  output [15:0] O
);

  Adder #(.width(16)) adder_1 (.a(16'h1), .b(A), .out(O));  // open: cin, cout
endmodule
