// Logisim project D_flip_flop.circ as structural Verilog: 1 circuit, main circuit main
module main (
  input  I,
  input  load,
  output O
);

  wire and_1_out, and_2_out, clock_1_out, multiplexer_1_out, nor_1_out, not_1_out;

  Multiplexer multiplexer_1 (.in0(O), .in1(I), .out(multiplexer_1_out), .sel(load));
  Clock clock_1 (.out(clock_1_out));
  not not_1 (not_1_out, multiplexer_1_out);
  and and_1 (and_1_out, multiplexer_1_out, clock_1_out);
  and and_2 (and_2_out, not_1_out, clock_1_out);
  nor nor_1 (nor_1_out, O, and_1_out);
  nor nor_2 (O, and_2_out, nor_1_out);
endmodule
