// Logisim project PC.circ as structural Verilog: 1 circuit, main circuit main
module main (
  input  [15:0] input_user,
  input  [15:0] zero_v,
  input  in_3,
  input  inc,
  input  load,
  input  reset,
  input  in_7,
  output [15:0] O
);

  wire clock_1_out;
  wire [15:0] adder_1_out, multiplexer_1_out, multiplexer_2_out, multiplexer_3_out;

  Adder #(.width(16)) adder_1 (.a(16'h1), .b(O), .out(adder_1_out));  // open: cin, cout
  Multiplexer #(.width(16)) multiplexer_1 (.in0(O), .in1(adder_1_out), .out(multiplexer_1_out), .sel(inc));
  Multiplexer #(.width(16)) multiplexer_2 (
    .in0(multiplexer_1_out), .in1(input_user), .out(multiplexer_2_out), .sel(load));
  Multiplexer #(.width(16)) multiplexer_3 (.in0(multiplexer_2_out), .in1(zero_v), .out(multiplexer_3_out), .sel(reset));
  Register #(.width(16)) register_1 (.D(multiplexer_3_out), .en(in_7), .Q(O), .clk(clock_1_out), .clr(in_3));
  Clock clock_1 (.out(clock_1_out));
endmodule
