// Logisim project Ram64k.circ as structural Verilog: 1 circuit, main circuit main
module main (
  input  [15:0] address,
  input  load,
  input  [15:0] DataBus,
  output [15:0] O
);

  wire clock_1_out;

  Clock clock_1 (.out(clock_1_out));
  RAM #(.addrWidth(16), .dataWidth(16), .enables("line"), .trigger("high")) Ram64k (
    .addr(address), .we(load), .clk(clock_1_out), .din(DataBus), .dout(O));
endmodule
