// Logisim project dff_register.circ as structural Verilog: 1 circuit, main circuit main
module main (
  input  I0,
  input  load,
  input  I1,
  input  I2,
  input  I3,
  input  I4,
  input  I5,
  input  I6,
  input  I7,
  input  I8,
  input  I9,
  input  I10,
  input  I11,
  input  I12,
  input  I13,
  input  I14,
  input  I15,
  output O0,
  output O1,
  output O2,
  output O3,
  output O4,
  output O5,
  output O6,
  output O7,
  output O8,
  output O9,
  output O10,
  output O11,
  output O12,
  output O13,
  output O14,
  output O15
);

  wire and_1_out, and_2_out, and_3_out, and_4_out, and_5_out, and_6_out, and_7_out, and_8_out, and_9_out,
       and_10_out, and_11_out, and_12_out, and_13_out, and_14_out, and_15_out, and_16_out, and_17_out,
       and_18_out, and_19_out, and_20_out, and_21_out, and_22_out, and_23_out, and_24_out, and_25_out,
       and_26_out, and_27_out, and_28_out, and_29_out, and_30_out, and_31_out, and_32_out, clock_1_out,
       multiplexer_1_out, multiplexer_2_out, multiplexer_3_out, multiplexer_4_out, multiplexer_5_out,
       multiplexer_6_out, multiplexer_7_out, multiplexer_8_out, multiplexer_9_out, multiplexer_10_out,
       multiplexer_11_out, multiplexer_12_out, multiplexer_13_out, multiplexer_14_out, multiplexer_15_out,
       multiplexer_16_out, nor_1_out, nor_3_out, nor_5_out, nor_7_out, nor_9_out, nor_11_out, nor_13_out,
       nor_15_out, nor_17_out, nor_19_out, nor_21_out, nor_23_out, nor_25_out, nor_27_out, nor_29_out,
       nor_31_out, not_1_out, not_2_out, not_3_out, not_4_out, not_5_out, not_6_out, not_7_out, not_8_out,
       not_9_out, not_10_out, not_11_out, not_12_out, not_13_out, not_14_out, not_15_out, not_16_out;

  Multiplexer multiplexer_1 (.in0(O0), .in1(I0), .out(multiplexer_1_out), .sel(load));
  Clock clock_1 (.out(clock_1_out));
  Multiplexer multiplexer_2 (.in0(O1), .in1(I1), .out(multiplexer_2_out), .sel(load));
  Multiplexer multiplexer_3 (.in0(O2), .in1(I2), .out(multiplexer_3_out), .sel(load));
  Multiplexer multiplexer_4 (.in0(O3), .in1(I3), .out(multiplexer_4_out), .sel(load));
  Multiplexer multiplexer_5 (.in0(O4), .in1(I4), .out(multiplexer_5_out), .sel(load));
  Multiplexer multiplexer_6 (.in0(O5), .in1(I5), .out(multiplexer_6_out), .sel(load));
  Multiplexer multiplexer_7 (.in0(O6), .in1(I6), .out(multiplexer_7_out), .sel(load));
  Multiplexer multiplexer_8 (.in0(O7), .in1(I7), .out(multiplexer_8_out), .sel(load));
  Multiplexer multiplexer_9 (.in0(O8), .in1(I8), .out(multiplexer_9_out), .sel(load));
  Multiplexer multiplexer_10 (.in0(O9), .in1(I9), .out(multiplexer_10_out), .sel(load));
  Multiplexer multiplexer_11 (.in0(O10), .in1(I10), .out(multiplexer_11_out), .sel(load));
  Multiplexer multiplexer_12 (.in0(O11), .in1(I11), .out(multiplexer_12_out), .sel(load));
  Multiplexer multiplexer_13 (.in0(O12), .in1(I12), .out(multiplexer_13_out), .sel(load));
  Multiplexer multiplexer_14 (.in0(O13), .in1(I13), .out(multiplexer_14_out), .sel(load));
  Multiplexer multiplexer_15 (.in0(O14), .in1(I14), .out(multiplexer_15_out), .sel(load));
  Multiplexer multiplexer_16 (.in0(O15), .in1(I15), .out(multiplexer_16_out), .sel(load));
  not not_1 (not_1_out, multiplexer_1_out);
  not not_2 (not_2_out, multiplexer_2_out);
  not not_3 (not_3_out, multiplexer_3_out);
  not not_4 (not_4_out, multiplexer_4_out);
  not not_5 (not_5_out, multiplexer_5_out);
  not not_6 (not_6_out, multiplexer_6_out);
  not not_7 (not_7_out, multiplexer_7_out);
  not not_8 (not_8_out, multiplexer_8_out);
  not not_9 (not_9_out, multiplexer_9_out);
  not not_10 (not_10_out, multiplexer_10_out);
  not not_11 (not_11_out, multiplexer_11_out);
  not not_12 (not_12_out, multiplexer_12_out);
  not not_13 (not_13_out, multiplexer_13_out);
  not not_14 (not_14_out, multiplexer_14_out);
  not not_15 (not_15_out, multiplexer_15_out);
  not not_16 (not_16_out, multiplexer_16_out);
  and and_1 (and_1_out, multiplexer_1_out, clock_1_out);
  and and_2 (and_2_out, multiplexer_2_out, clock_1_out);
  and and_3 (and_3_out, multiplexer_3_out, clock_1_out);
  and and_4 (and_4_out, multiplexer_4_out, clock_1_out);
  and and_5 (and_5_out, multiplexer_5_out, clock_1_out);
  and and_6 (and_6_out, multiplexer_6_out, clock_1_out);
  and and_7 (and_7_out, multiplexer_7_out, clock_1_out);
  and and_8 (and_8_out, multiplexer_8_out, clock_1_out);
  and and_9 (and_9_out, multiplexer_9_out, clock_1_out);
  and and_10 (and_10_out, multiplexer_10_out, clock_1_out);
  and and_11 (and_11_out, multiplexer_11_out, clock_1_out);
  and and_12 (and_12_out, multiplexer_12_out, clock_1_out);
  and and_13 (and_13_out, multiplexer_13_out, clock_1_out);
  and and_14 (and_14_out, multiplexer_14_out, clock_1_out);
  and and_15 (and_15_out, multiplexer_15_out, clock_1_out);
  and and_16 (and_16_out, multiplexer_16_out, clock_1_out);
  and and_17 (and_17_out, not_1_out, clock_1_out);
  and and_18 (and_18_out, not_2_out, clock_1_out);
  and and_19 (and_19_out, not_3_out, clock_1_out);
  and and_20 (and_20_out, not_4_out, clock_1_out);
  and and_21 (and_21_out, not_5_out, clock_1_out);
  and and_22 (and_22_out, not_6_out, clock_1_out);
  and and_23 (and_23_out, not_7_out, clock_1_out);
  and and_24 (and_24_out, not_8_out, clock_1_out);
  and and_25 (and_25_out, not_9_out, clock_1_out);
  and and_26 (and_26_out, not_10_out, clock_1_out);
  and and_27 (and_27_out, not_11_out, clock_1_out);
  and and_28 (and_28_out, not_12_out, clock_1_out);
  and and_29 (and_29_out, not_13_out, clock_1_out);
  and and_30 (and_30_out, not_14_out, clock_1_out);
  and and_31 (and_31_out, not_15_out, clock_1_out);
  and and_32 (and_32_out, not_16_out, clock_1_out);
  nor nor_1 (nor_1_out, O0, and_1_out);
  nor nor_2 (O0, and_17_out, nor_1_out);
  nor nor_3 (nor_3_out, O1, and_2_out);
  nor nor_4 (O1, and_18_out, nor_3_out);
  nor nor_5 (nor_5_out, O2, and_3_out);
  nor nor_6 (O2, and_19_out, nor_5_out);
  nor nor_7 (nor_7_out, O3, and_4_out);
  nor nor_8 (O3, and_20_out, nor_7_out);
  nor nor_9 (nor_9_out, O4, and_5_out);
  nor nor_10 (O4, and_21_out, nor_9_out);
  nor nor_11 (nor_11_out, O5, and_6_out);
  nor nor_12 (O5, and_22_out, nor_11_out);
  nor nor_13 (nor_13_out, O6, and_7_out);
  nor nor_14 (O6, and_23_out, nor_13_out);
  nor nor_15 (nor_15_out, O7, and_8_out);
  nor nor_16 (O7, and_24_out, nor_15_out);
  nor nor_17 (nor_17_out, O8, and_9_out);
  nor nor_18 (O8, and_25_out, nor_17_out);
  nor nor_19 (nor_19_out, O9, and_10_out);
  nor nor_20 (O9, and_26_out, nor_19_out);
  nor nor_21 (nor_21_out, O10, and_11_out);
  nor nor_22 (O10, and_27_out, nor_21_out);
  nor nor_23 (nor_23_out, O11, and_12_out);
  nor nor_24 (O11, and_28_out, nor_23_out);
  nor nor_25 (nor_25_out, O12, and_13_out);
  nor nor_26 (O12, and_29_out, nor_25_out);
  nor nor_27 (nor_27_out, O13, and_14_out);
  nor nor_28 (O13, and_30_out, nor_27_out);
  nor nor_29 (nor_29_out, O14, and_15_out);
  nor nor_30 (O14, and_31_out, nor_29_out);
  nor nor_31 (nor_31_out, O15, and_16_out);
  nor nor_32 (O15, and_32_out, nor_31_out);
endmodule
