// Logisim project CPU.circ as structural Verilog: 1 circuit, main circuit main
module main (
  input  [15:0] falsex,
  input  [15:0] instruction,
  input  [15:0] inM,
  input  [15:0] falsey,
  input  [15:0] false,
  input  reset,
  input  in_7,
  input  Inc,
  output [15:0] outM,
  output zr,
  output ng,
  output [15:0] AddressM,
  output [15:0] PC,
  output writeM
);

  wire and_1_out, and_2_out, and_6_out, and_7_out, and_8_out, and_9_out, and_10_out, and_11_out, and_12_out,
       clock_1_out, not_1_out, not_5_out, not_7_out, or_1_out, or_2_out, or_3_out, or_4_out, or_5_out,
       or_6_out;
  wire [15:0] adder_1_out, adder_2_out, and_3_out, and_4_out, and_5_out, multiplexer_1_out,
       multiplexer_2_out, multiplexer_3_out, multiplexer_4_out, multiplexer_5_out, multiplexer_6_out,
       multiplexer_7_out, multiplexer_8_out, multiplexer_9_out, multiplexer_10_out, not_2_out, not_3_out,
       not_4_out, register_3_q;

  not not_1 (not_1_out, instruction[15]);
  and and_1 (and_1_out, instruction[12], instruction[15]);
  Clock clock_1 (.out(clock_1_out));
  Multiplexer #(.width(16)) multiplexer_1 (
    .in0({ng, outM[14:0]}), .in1(instruction), .out(multiplexer_1_out), .sel(not_1_out));
  or or_1 (or_1_out, instruction[5], not_1_out);
  Adder #(.width(16)) adder_1 (.a(16'h1), .b(PC), .out(adder_1_out));  // open: cin, cout
  Register #(.width(16)) register_1 (
    .D(multiplexer_1_out), .en(or_1_out), .clk(clock_1_out), .Q(AddressM));  // open: clr
  Multiplexer #(.width(16)) multiplexer_2 (.in0(PC), .in1(adder_1_out), .out(multiplexer_2_out), .sel(Inc));
  Multiplexer #(.width(16)) multiplexer_3 (
    .in0(multiplexer_2_out), .in1(AddressM), .out(multiplexer_3_out), .sel(or_6_out));
  and and_2 (and_2_out, instruction[15], instruction[4]);
  Multiplexer #(.width(16)) multiplexer_4 (.in0(multiplexer_3_out), .in1(false), .out(multiplexer_4_out), .sel(reset));
  Register #(.width(16)) register_2 (.D(multiplexer_4_out), .en(1'b1), .Q(PC), .clk(clock_1_out), .clr(in_7));
  Register #(.width(16)) register_3 (
    .D({ng, outM[14:0]}), .en(and_2_out), .clk(clock_1_out), .Q(register_3_q));  // open: clr
  Multiplexer #(.width(16)) multiplexer_5 (.in0(AddressM), .in1(inM), .out(multiplexer_5_out), .sel(and_1_out));
  assign and_3_out = register_3_q & falsex;  // AND_Gate and_3, 16 bits wide
  assign and_4_out = multiplexer_5_out & falsey;  // AND_Gate and_4, 16 bits wide
  Multiplexer #(.width(16)) multiplexer_6 (
    .in0(register_3_q), .in1(and_3_out), .out(multiplexer_6_out), .sel(instruction[11]));
  Multiplexer #(.width(16)) multiplexer_7 (
    .in0(multiplexer_5_out), .in1(and_4_out), .out(multiplexer_7_out), .sel(instruction[9]));
  assign not_2_out = ~multiplexer_6_out;  // NOT_Gate not_2, 16 bits wide
  assign not_3_out = ~multiplexer_7_out;  // NOT_Gate not_3, 16 bits wide
  Multiplexer #(.width(16)) multiplexer_8 (
    .in0(multiplexer_6_out), .in1(not_2_out), .out(multiplexer_8_out), .sel(instruction[10]));
  Multiplexer #(.width(16)) multiplexer_9 (
    .in0(multiplexer_7_out), .in1(not_3_out), .out(multiplexer_9_out), .sel(instruction[8]));
  assign and_5_out = multiplexer_8_out & multiplexer_9_out;  // AND_Gate and_5, 16 bits wide
  Adder #(.width(16)) adder_2 (.a(multiplexer_8_out), .b(multiplexer_9_out), .out(adder_2_out));  // open: cin, cout
  Multiplexer #(.width(16)) multiplexer_10 (
    .in0(and_5_out), .in1(adder_2_out), .out(multiplexer_10_out), .sel(instruction[7]));
  assign not_4_out = ~multiplexer_10_out;  // NOT_Gate not_4, 16 bits wide
  and and_6 (and_6_out, instruction[15], instruction[0]);
  and and_7 (and_7_out, instruction[1], instruction[15]);
  and and_8 (and_8_out, instruction[2], instruction[15]);
  Multiplexer #(.width(16)) multiplexer_11 (
    .in0(multiplexer_10_out), .in1(not_4_out), .out({ng, outM[14:0]}), .sel(instruction[6]));
  or or_2 (or_2_out, outM[0], outM[1], outM[2], outM[3], outM[4], outM[5], outM[6], outM[7]);
  or or_3 (or_3_out, outM[8], outM[9], outM[10], outM[11], outM[12], outM[13], outM[14], ng);
  or or_4 (or_4_out, or_2_out, or_3_out);
  not not_5 (not_5_out, ng);
  not not_6 (zr, or_4_out);
  not not_7 (not_7_out, zr);
  and and_9 (and_9_out, not_5_out, not_7_out);
  and and_10 (and_10_out, and_7_out, zr);
  and and_11 (and_11_out, and_8_out, ng);
  and and_12 (and_12_out, and_9_out, and_6_out);
  or or_5 (or_5_out, and_12_out, and_10_out);
  or or_6 (or_6_out, or_5_out, and_11_out);
  and and_13 (writeM, instruction[3], instruction[15]);

  assign outM[15] = ng;
endmodule
