// Logisim project Memory.circ as structural Verilog: 1 circuit, main circuit main
module main (
  input  [14:0] in_1,
  input  [14:0] in_2,
  input  in_3,
  input  [15:0] in_4,
  output [15:0] out_5,
  output [15:0] out_6
);

  wire clock_1_out;

  Clock clock_1 (.out(clock_1_out));
  ROM #(.addrWidth(15), .dataWidth(16)) rom_1 (.addr(in_1), .data(out_5));
  RAM #(.addrWidth(15), .dataWidth(16), .enables("line")) ram_1 (
    .addr(in_2), .we(in_3), .clk(clock_1_out), .din(in_4), .dout(out_6));

  // Notes on the sheet:
  //   contents of rom_1 (hex, n*v repeats v):
  //   afda dddd ffff 0 a a ad aff
endmodule
