// Logisim project AuthorsComputer.circ as structural Verilog: 3 circuits, main circuit main
module main (
  input  [15:0] STOP_ADDRESS,
  input  MEASURE,
  input  STAT_RESET,
  input  STOP_ENABLE,
  input  [15:0] falsex,
  input  [15:0] falsey,
  input  [15:0] in_7,
  input  reset,
  input  in_9,
  output [31:0] ExecutionCycles,
  output [31:0] DynamicInstructions,
  output [31:0] DynamicBranchCount,
  output [31:0] MemoryReads,
  output [31:0] MemoryWrites,
  output [15:0] PC_VALUE,
  output HALTED,
  output [15:0] outM,
  output zr,
  output ng
);

  wire A_EN, A_REQ, and_6_out, and_7_out, and_8_out, and_9_out, and_11_out, and_12_out, and_13_out, D_EN,
       D_REQ, MEAS_EN, not_1_out, not_5_out, not_7_out, or_2_out, or_3_out, or_4_out, or_5_out, PC_EN,
       RAM_EN, RAM_REQ, STAT_CLK, STAT_JUMP_TAKEN, STAT_READ_M;
  wire [15:0] adder_1_out, adder_2_out, and_3_out, and_4_out, and_5_out, multiplexer_1_out,
       multiplexer_2_out, multiplexer_3_out, multiplexer_4_out, multiplexer_5_out, multiplexer_6_out,
       multiplexer_7_out, multiplexer_8_out, multiplexer_9_out, multiplexer_10_out, not_2_out, not_3_out,
       not_4_out, ram_1_dout, register_1_q, register_3_q, rom_1_data;

  ROM #(.addrWidth(16), .dataWidth(16)) rom_1 (.addr(PC_VALUE), .data(rom_1_data));
  not not_1 (not_1_out, rom_1_data[15]);
  and and_1 (STAT_READ_M, rom_1_data[12], rom_1_data[15]);
  Clock clock_1 (.out(STAT_CLK));
  Multiplexer #(.width(16)) multiplexer_1 (
    .in0({ng, outM[14:0]}), .in1(rom_1_data), .out(multiplexer_1_out), .sel(not_1_out));
  Statistics statistics_1 (
    .CLK(STAT_CLK), .MEASURE(MEAS_EN), .STAT_RESET(STAT_RESET), .CPU_RESET(reset), .PC_CLEAR(in_9),
    .READ_M(STAT_READ_M), .WRITE_M(RAM_REQ), .JUMP_TAKEN(STAT_JUMP_TAKEN), .out_12(MemoryReads),
    .out_13(MemoryWrites), .out_9(ExecutionCycles), .out_10(DynamicInstructions), .out_11(DynamicBranchCount));
  or or_1 (A_REQ, rom_1_data[5], not_1_out);
  Register #(.width(16)) register_1 (.D(multiplexer_1_out), .en(A_EN), .clk(STAT_CLK), .Q(register_1_q));  // open: clr
  Adder #(.width(16)) adder_1 (.a(16'h1), .b(PC_VALUE), .out(adder_1_out));  // open: cin, cout
  Multiplexer #(.width(16)) multiplexer_2 (.in0(PC_VALUE), .in1(adder_1_out), .out(multiplexer_2_out), .sel(1'b1));
  Multiplexer #(.width(16)) multiplexer_3 (
    .in0(multiplexer_2_out), .in1(register_1_q), .out(multiplexer_3_out), .sel(STAT_JUMP_TAKEN));
  and and_2 (D_REQ, rom_1_data[15], rom_1_data[4]);
  Multiplexer #(.width(16)) multiplexer_4 (.in0(multiplexer_3_out), .in1(in_7), .out(multiplexer_4_out), .sel(reset));
  Register #(.width(16)) register_2 (.D(multiplexer_4_out), .en(PC_EN), .Q(PC_VALUE), .clk(STAT_CLK), .clr(in_9));
  Register #(.width(16)) register_3 (.D({ng, outM[14:0]}), .en(D_EN), .clk(STAT_CLK), .Q(register_3_q));  // open: clr
  Multiplexer #(.width(16)) multiplexer_5 (
    .in0(register_1_q), .in1(ram_1_dout), .out(multiplexer_5_out), .sel(STAT_READ_M));
  HaltControl haltcontrol_1 (
    .PC(PC_VALUE), .StopAddress(STOP_ADDRESS), .Enabled(STOP_ENABLE), .ResetCPU(reset), .LoadA(A_REQ),
    .LoadD(D_REQ), .LoadPC(1'b1), .WriteRAM(RAM_REQ), .Measure(MEASURE), .Halted(HALTED), .EnableA(A_EN),
    .out_12(D_EN), .EnablePC(PC_EN), .EnableRAM(RAM_EN), .MeasureOut(MEAS_EN));
  assign and_3_out = register_3_q & falsex;  // AND_Gate and_3, 16 bits wide
  assign and_4_out = multiplexer_5_out & falsey;  // AND_Gate and_4, 16 bits wide
  Multiplexer #(.width(16)) multiplexer_6 (
    .in0(register_3_q), .in1(and_3_out), .out(multiplexer_6_out), .sel(rom_1_data[11]));
  Multiplexer #(.width(16)) multiplexer_7 (
    .in0(multiplexer_5_out), .in1(and_4_out), .out(multiplexer_7_out), .sel(rom_1_data[9]));
  assign not_2_out = ~multiplexer_6_out;  // NOT_Gate not_2, 16 bits wide
  assign not_3_out = ~multiplexer_7_out;  // NOT_Gate not_3, 16 bits wide
  Multiplexer #(.width(16)) multiplexer_8 (
    .in0(multiplexer_6_out), .in1(not_2_out), .out(multiplexer_8_out), .sel(rom_1_data[10]));
  Multiplexer #(.width(16)) multiplexer_9 (
    .in0(multiplexer_7_out), .in1(not_3_out), .out(multiplexer_9_out), .sel(rom_1_data[8]));
  assign and_5_out = multiplexer_8_out & multiplexer_9_out;  // AND_Gate and_5, 16 bits wide
  Adder #(.width(16)) adder_2 (.a(multiplexer_8_out), .b(multiplexer_9_out), .out(adder_2_out));  // open: cin, cout
  Multiplexer #(.width(16)) multiplexer_10 (
    .in0(and_5_out), .in1(adder_2_out), .out(multiplexer_10_out), .sel(rom_1_data[7]));
  and and_6 (and_6_out, rom_1_data[15], rom_1_data[0]);
  and and_7 (and_7_out, rom_1_data[1], rom_1_data[15]);
  and and_8 (and_8_out, rom_1_data[15], rom_1_data[2]);
  assign not_4_out = ~multiplexer_10_out;  // NOT_Gate not_4, 16 bits wide
  Multiplexer #(.width(16)) multiplexer_11 (
    .in0(multiplexer_10_out), .in1(not_4_out), .out({ng, outM[14:0]}), .sel(rom_1_data[6]));
  and and_9 (and_9_out, not_7_out, not_5_out);
  and and_10 (RAM_REQ, rom_1_data[3], rom_1_data[15]);
  and and_11 (and_11_out, and_9_out, and_6_out);
  and and_12 (and_12_out, and_7_out, zr);
  and and_13 (and_13_out, and_8_out, ng);
  or or_2 (or_2_out, outM[0], outM[1], outM[2], outM[3], outM[4], outM[5], outM[6], outM[7]);
  or or_3 (or_3_out, outM[8], outM[9], outM[10], outM[11], outM[12], outM[13], outM[14], ng);
  or or_4 (or_4_out, or_2_out, or_3_out);
  not not_5 (not_5_out, ng);
  or or_5 (or_5_out, and_11_out, and_12_out);
  not not_6 (zr, or_4_out);
  not not_7 (not_7_out, zr);
  or or_6 (STAT_JUMP_TAKEN, or_5_out, and_13_out);
  RAM #(.addrWidth(16), .dataWidth(16), .enables("line")) ram_1 (
    .addr(register_1_q), .we(RAM_EN), .clk(STAT_CLK), .din({ng, outM[14:0]}), .dout(ram_1_dout));

  assign outM[15] = ng;

  // Other names for the same wires on the sheet: MEAS_REQ = MEASURE; PC_BUS[15:0] = PC_VALUE; STAT_CPU_RESET = reset;
  //   STAT_PC_CLEAR = in_9; STAT_WRITE_M = RAM_REQ; STOP_ADDR[15:0] = STOP_ADDRESS; STOP_ON = STOP_ENABLE;
  //   STOPPED = HALTED

  // Notes on the sheet:
  //   contents of rom_1 (hex, n*v repeats v):
  //   7 ec10 10 e308 10 fc10 3f e302 13 ea88 100 ec10 11 e308 10 fc10 12 e308 11 fc20 fc10 14 e308 11 fc20
  //   ede0 fc10 15 e308 14 fc10 15 f4d0 30 e306 15 fc10 11 fc20 e308 14 fc10 11 fc20 ede0 e308 13 efc8 11
  //   fdc8 12 fc88 fc10 12 e301 13 fc10 3f e302 10 fc88 4 ea87
  //   1. STATISTICS
  //   SETUP (automatic ticks OFF)
  //   1. Load ROM; choose STOP_ADDRESS and STOP_ENABLE.
  //   2. reset = 1; advance one full clock cycle; reset = 0.
  //   3. STAT_RESET = 1, then 0. Set MEASURE = 1.
  //   4. Run. HALTED = 1 freezes CPU state and statistics.
  //   To restart: stop automatic ticks and repeat steps 2-3.
  //   Reads: C-instructions selecting M; instruction fetches excluded.
  //   Writes: RAM write operations. Jumps: taken jumps.
  //   Single-cycle CPU: Cycles = Instructions.
  //   32-bit counters wrap at 2^32.
  //   2. PROGRAM STOP
  //   STOP_ADDRESS: first address NOT executed.
  //   HEX example: decimal 20 = 0014.
  //   STOP_ENABLE: 1 = on, 0 = off.
  //   HALTED: 1 = stopped; counters hold.
  //   3. STOP CONTROLLER
  //   Open HaltControl to inspect the logic.
  //   Clock is unchanged. Register and write enables are gated.
endmodule

module Statistics (
  input  CLK,
  input  MEASURE,
  input  STAT_RESET,
  input  CPU_RESET,
  input  PC_CLEAR,
  input  READ_M,
  input  WRITE_M,
  input  JUMP_TAKEN,
  output [31:0] out_9,
  output [31:0] out_10,
  output [31:0] out_11,
  output [31:0] out_12,
  output [31:0] out_13
);

  wire and_1_out, and_2_out, and_3_out, not_1_out, or_1_out, RUN;

  and and_1 (and_1_out, RUN, JUMP_TAKEN);
  and and_2 (and_2_out, RUN, READ_M);
  and and_3 (and_3_out, RUN, WRITE_M);
  or or_1 (or_1_out, CPU_RESET, PC_CLEAR);
  not not_1 (not_1_out, or_1_out);
  and and_4 (RUN, not_1_out, MEASURE);
  Counter #(.max('hffffffff), .width(32)) ExecutionCycles (
    .load(1'b0), .D({32{1'b0}}), .count(RUN), .Q(out_9), .up(1'b1), .clk(CLK), .clr(STAT_RESET));  // open: carry
  Counter #(.max('hffffffff), .width(32)) DynamicInstructions (
    .load(1'b0), .D({32{1'b0}}), .count(RUN), .Q(out_10), .up(1'b1), .clk(CLK), .clr(STAT_RESET));  // open: carry
  Counter #(.max('hffffffff), .width(32)) TakenJumps (
    .load(1'b0), .D({32{1'b0}}), .count(and_1_out), .Q(out_11), .up(1'b1), .clk(CLK), .clr(STAT_RESET));  // open: carry
  Counter #(.max('hffffffff), .width(32)) MemoryReads (
    .load(1'b0), .D({32{1'b0}}), .count(and_2_out), .Q(out_12), .up(1'b1), .clk(CLK), .clr(STAT_RESET));  // open: carry
  Counter #(.max('hffffffff), .width(32)) MemoryWrites (
    .load(1'b0), .D({32{1'b0}}), .count(and_3_out), .Q(out_13), .up(1'b1), .clk(CLK), .clr(STAT_RESET));  // open: carry

  // Notes on the sheet:
  //   Rising-edge counters. RUN = MEASURE AND NOT(CPU_RESET OR PC_CLEAR). Reset has priority.
endmodule

module HaltControl (
  input  [15:0] PC,
  input  [15:0] StopAddress,
  input  Enabled,
  input  ResetCPU,
  input  LoadA,
  input  LoadD,
  input  LoadPC,
  input  WriteRAM,
  input  Measure,
  output Halted,
  output EnableA,
  output out_12,
  output EnablePC,
  output EnableRAM,
  output MeasureOut
);

  wire Equal, Run, RunOrReset;

  Comparator #(.width(16)) comparator_1 (.a(PC), .b(StopAddress), .eq(Equal));  // open: gt, lt
  and and_1 (Halted, Equal, Enabled);
  not not_1 (Run, Halted);
  and and_2 (EnableA, LoadA, Run);
  and and_3 (out_12, LoadD, Run);
  and and_4 (EnableRAM, WriteRAM, Run);
  and and_5 (MeasureOut, Measure, Run);
  or or_1 (RunOrReset, Run, ResetCPU);
  and and_6 (EnablePC, LoadPC, RunOrReset);

  // Other names for the same wires on the sheet: EnableD_t = out_12

  // Notes on the sheet:
  //   INPUTS
  //   STOP DETECTION
  //   EXECUTION ENABLES
  //   RESET CAN RESTART A HALTED CPU
  //   OUTPUTS
endmodule
