// Logisim project BasicComputerStats.circ as structural Verilog: 2 circuits, main circuit CompleteComputer
module CompleteComputer (
  input  STAT_RESET,
  input  MEASURE,
  output [31:0] ExecutionCycles,
  output [31:0] DynamicInstructions,
  output [31:0] DynamicBranchCount,
  output [31:0] MemoryReads,
  output [31:0] MemoryWrites
);

  wire and_2_out, and_3_out, and_4_out, and_5_out, and_6_out, bit16_alsu_1_p5, bit16_alsu_1_p6,
       control_unit_1_p3, control_unit_1_p7, control_unit_1_p8, control_unit_1_p9, control_unit_1_p10,
       control_unit_1_p11, control_unit_1_p12, control_unit_1_p13, control_unit_1_p14, control_unit_1_p15,
       control_unit_1_p16, control_unit_1_p17, control_unit_1_p19, control_unit_1_p22, CP_out, FGI_p3,
       FGO_p4, IEN_p1, IEN_p3, IR_p4, keyboard_1_avail, not_1_out, or_1_out, OUTR_p2, PC_p3, PC_p4, R_p1,
       R_p3, S_p1, S_p4, S_p5, STAT_CP, STAT_DRINC, STAT_IRLD, STAT_PCLD, STAT_READ, STAT_SCCLR, STAT_WRITE,
       TR_p2, TR_p3, TR_p4, undriven, undriven_2, undriven_3, undriven_4, undriven_5, undriven_6, undriven_7,
       undriven_8, undriven_9;
  wire [3:0] AR_p1, AR_p1_2, AR_p1_3, control_unit_1_p1, control_unit_1_p2, control_unit_1_p2_2,
       control_unit_1_p2_3, control_unit_1_p2_4, control_unit_1_p4, control_unit_1_p4_2, control_unit_1_p4_3,
       control_unit_1_p4_4, control_unit_1_p6, control_unit_1_p6_2, control_unit_1_p6_3, control_unit_1_p6_4,
       control_unit_1_p18, DR_p1, INPR_p6, INPR_p6_2;
  wire [6:0] keyboard_1_data;
  wire [7:0] OUTR_p6;
  wire [11:0] AR_p6, PC_p6;
  wire [15:0] multiplexer_1_out, ram_1_dout, TR_p6;

  Multiplexer #(.width(16)) multiplexer_1 (
    .in0({control_unit_1_p4_4, control_unit_1_p4_3, control_unit_1_p4_2, control_unit_1_p4}),
    .in1({{8{1'b0}}, INPR_p6_2, INPR_p6}), .out(multiplexer_1_out), .sel(FGI_p3));
  Clock CP (.out(CP_out));
  and and_1 (STAT_CP, S_p5, CP_out);
  // Bit4_Register bit4_register_1: pin names not known; wires that end beside it: 1'b0, 1'b0, STAT_CP, STAT_SCCLR, 1'b1
  Hex_Digit_Display hex_digit_display_1 (.value(control_unit_1_p1));  // open: dp
  // Control_Unit control_unit_1: pin names not known; wires that end beside it: control_unit_1_p1, {control_unit_1_p2_4, control_unit_1_p2_3, control_unit_1_p2_2, control_unit_1_p2}, control_unit_1_p3, {control_unit_1_p4_4, control_unit_1_p4_3, control_unit_1_p4_2, control_unit_1_p4}, STAT_SCCLR, {control_unit_1_p6_4, control_unit_1_p6_3, control_unit_1_p6_2, control_unit_1_p6}, control_unit_1_p7, control_unit_1_p8, control_unit_1_p9, control_unit_1_p10, control_unit_1_p11, control_unit_1_p12, control_unit_1_p13, control_unit_1_p14, control_unit_1_p15, control_unit_1_p16, control_unit_1_p17, control_unit_1_p18, control_unit_1_p19, 1'b0, STAT_DRINC, control_unit_1_p22, STAT_IRLD
  Hex_Digit_Display hex_digit_display_2 (.value(control_unit_1_p18));  // open: dp
  // Bit16_ALSU bit16_alsu_1: pin names not known; wires that end beside it: multiplexer_1_out, {control_unit_1_p6_4, control_unit_1_p6_3, control_unit_1_p6_2, control_unit_1_p6}, control_unit_1_p1, control_unit_1_p3, bit16_alsu_1_p5, bit16_alsu_1_p6
  Keyboard #(.buflen(8)) keyboard_1 (
    .clk(STAT_CP), .re(FGI_p3), .avail(keyboard_1_avail), .data(keyboard_1_data));  // open: clr
  RAM #(.addrWidth(12), .asyncread("true"), .dataWidth(16)) ram_1 (
    .addr(AR_p6), .we(STAT_WRITE), .oe(STAT_READ), .clk(STAT_CP), .din({DR_p1, AR_p1_3, AR_p1_2, AR_p1}),
    .dout(ram_1_dout));
  // Bit12_Register AR: pin names not known; wires that end beside it: {AR_p1_3, AR_p1_2, AR_p1}, control_unit_1_p13, control_unit_1_p15, control_unit_1_p17, STAT_CP, AR_p6
  Hex_Digit_Display hex_digit_display_3 (.value(AR_p6[11:8]));  // open: dp
  // Bit12_Register PC: pin names not known; wires that end beside it: {AR_p1_3, AR_p1_2, AR_p1}, STAT_PCLD, PC_p3, PC_p4, STAT_CP, PC_p6
  Hex_Digit_Display hex_digit_display_4 (.value(PC_p6[11:8]));  // open: dp
  // Bit16_Register DR: pin names not known; wires that end beside it: {DR_p1, AR_p1_3, AR_p1_2, AR_p1}, control_unit_1_p19, STAT_DRINC, control_unit_1_p22, STAT_CP, {control_unit_1_p4_4, control_unit_1_p4_3, control_unit_1_p4_2, control_unit_1_p4}
  Hex_Digit_Display hex_digit_display_5 (.value(control_unit_1_p4_4));  // open: dp
  // Bit16_Register AC: pin names not known; wires that end beside it: bit16_alsu_1_p5, control_unit_1_p7, control_unit_1_p9, control_unit_1_p11, STAT_CP, {control_unit_1_p6_4, control_unit_1_p6_3, control_unit_1_p6_2, control_unit_1_p6}
  Hex_Digit_Display hex_digit_display_6 (.value(control_unit_1_p6_4));  // open: dp
  // Bit8_Register INPR: pin names not known; wires that end beside it: {1'b0, keyboard_1_data}, keyboard_1_avail, 1'b0, 1'b0, STAT_CP, {INPR_p6_2, INPR_p6}
  Hex_Digit_Display hex_digit_display_7 (.value(INPR_p6_2));  // open: dp
  // Bit16_Register IR: pin names not known; wires that end beside it: {DR_p1, AR_p1_3, AR_p1_2, AR_p1}, STAT_IRLD, 1'b0, IR_p4, STAT_CP, {control_unit_1_p2_4, control_unit_1_p2_3, control_unit_1_p2_2, control_unit_1_p2}
  Hex_Digit_Display hex_digit_display_8 (.value(control_unit_1_p2_4));  // open: dp
  // Bit16_Register TR: pin names not known; wires that end beside it: {DR_p1, AR_p1_3, AR_p1_2, AR_p1}, TR_p2, TR_p3, TR_p4, STAT_CP, TR_p6
  Hex_Digit_Display hex_digit_display_9 (.value(TR_p6[15:12]));  // open: dp
  // Bit8_Register OUTR: pin names not known; wires that end beside it: {AR_p1_2, AR_p1}, OUTR_p2, 1'b0, 1'b0, STAT_CP, OUTR_p6
  // Master_Slave_Flip_Flop IEN: pin names not known; wires that end beside it: IEN_p1, STAT_CP, IEN_p3, control_unit_1_p12
  // Master_Slave_Flip_Flop S: pin names not known; wires that end beside it: S_p1, STAT_CP, 1'b0, S_p4, S_p5
  // Master_Slave_Flip_Flop R: pin names not known; wires that end beside it: R_p1, STAT_CP, R_p3, control_unit_1_p8
  // Master_Slave_Flip_Flop FGI: pin names not known; wires that end beside it: keyboard_1_avail, STAT_CP, FGI_p3, control_unit_1_p14
  // Master_Slave_Flip_Flop FGO: pin names not known; wires that end beside it: OUTR_p2, STAT_CP, 1'b1, FGO_p4, control_unit_1_p16
  E_Register E (
    .ELD(undriven), .ALU_E(bit16_alsu_1_p6), .ECMP(undriven_3), .ECLR(undriven_2), .CP(STAT_CP),
    .E(control_unit_1_p10));
  Hex_Digit_Display hex_digit_display_10 (.value(ram_1_dout[15:12]));  // open: dp
  Hex_Digit_Display hex_digit_display_11 (.value(ram_1_dout[11:8]));  // open: dp
  Hex_Digit_Display hex_digit_display_12 (.value(AR_p6[7:4]));  // open: dp
  Hex_Digit_Display hex_digit_display_13 (.value(AR_p6[3:0]));  // open: dp
  Hex_Digit_Display hex_digit_display_14 (.value(PC_p6[7:4]));  // open: dp
  Hex_Digit_Display hex_digit_display_15 (.value(PC_p6[3:0]));  // open: dp
  Hex_Digit_Display hex_digit_display_16 (.value(control_unit_1_p4_3));  // open: dp
  Hex_Digit_Display hex_digit_display_17 (.value(control_unit_1_p4_2));  // open: dp
  Hex_Digit_Display hex_digit_display_18 (.value(control_unit_1_p6_3));  // open: dp
  Hex_Digit_Display hex_digit_display_19 (.value(control_unit_1_p6_2));  // open: dp
  Hex_Digit_Display hex_digit_display_20 (.value(INPR_p6));  // open: dp
  Hex_Digit_Display hex_digit_display_21 (.value(control_unit_1_p2_3));  // open: dp
  Hex_Digit_Display hex_digit_display_22 (.value(control_unit_1_p2_2));  // open: dp
  Hex_Digit_Display hex_digit_display_23 (.value(TR_p6[11:8]));  // open: dp
  Hex_Digit_Display hex_digit_display_24 (.value(TR_p6[7:4]));  // open: dp
  TTY #(.cols(8)) tty_1 (.data(OUTR_p6[6:0]), .clk(STAT_CP), .we(FGO_p4));  // open: clr
  LED Done (.in(S_p4));
  Hex_Digit_Display hex_digit_display_25 (.value(ram_1_dout[7:4]));  // open: dp
  Hex_Digit_Display hex_digit_display_26 (.value(ram_1_dout[3:0]));  // open: dp
  Hex_Digit_Display hex_digit_display_27 (.value(control_unit_1_p4));  // open: dp
  Hex_Digit_Display hex_digit_display_28 (.value(control_unit_1_p6));  // open: dp
  Hex_Digit_Display hex_digit_display_29 (.value(control_unit_1_p2));  // open: dp
  Hex_Digit_Display hex_digit_display_30 (.value(TR_p6[3:0]));  // open: dp
  assign {AR_p1_3, AR_p1_2, AR_p1} = undriven_4 ? AR_p6 : 12'bz;  // Controlled_Buffer controlled_buffer_1
  assign {AR_p1_3, AR_p1_2, AR_p1} = undriven_5 ? PC_p6 : 12'bz;  // Controlled_Buffer controlled_buffer_2
  assign {DR_p1, AR_p1_3, AR_p1_2, AR_p1} = undriven_6 ? {control_unit_1_p4_4, control_unit_1_p4_3, control_unit_1_p4_2, control_unit_1_p4} : 16'bz;  // Controlled_Buffer controlled_buffer_3
  Hex_Digit_Display hex_digit_display_31 (.value(DR_p1));  // open: dp
  Hex_Digit_Display hex_digit_display_32 (.value(AR_p1_3));  // open: dp
  assign {DR_p1, AR_p1_3, AR_p1_2, AR_p1} = undriven_7 ? {control_unit_1_p6_4, control_unit_1_p6_3, control_unit_1_p6_2, control_unit_1_p6} : 16'bz;  // Controlled_Buffer controlled_buffer_4
  Hex_Digit_Display hex_digit_display_33 (.value(AR_p1_2));  // open: dp
  Hex_Digit_Display hex_digit_display_34 (.value(AR_p1));  // open: dp
  assign {DR_p1, AR_p1_3, AR_p1_2, AR_p1} = undriven_8 ? {control_unit_1_p2_4, control_unit_1_p2_3, control_unit_1_p2_2, control_unit_1_p2} : 16'bz;  // Controlled_Buffer controlled_buffer_5
  assign {DR_p1, AR_p1_3, AR_p1_2, AR_p1} = STAT_READ ? ram_1_dout : 16'bz;  // Controlled_Buffer controlled_buffer_6
  assign {DR_p1, AR_p1_3, AR_p1_2, AR_p1} = undriven_9 ? TR_p6 : 16'bz;  // Controlled_Buffer controlled_buffer_7
  assign DR_p1 = undriven_5 ? 4'b0000 : 4'bz;  // Controlled_Buffer controlled_buffer_8
  or or_1 (or_1_out, STAT_PCLD, STAT_DRINC);
  not not_1 (not_1_out, STAT_IRLD);
  and and_2 (and_2_out, MEASURE, STAT_SCCLR);
  and and_3 (and_3_out, STAT_READ, not_1_out);
  and and_4 (and_4_out, MEASURE, STAT_WRITE);
  and and_5 (and_5_out, MEASURE, or_1_out);
  and and_6 (and_6_out, MEASURE, and_3_out);
  Counter #(.max('hffffffff), .trigger("falling"), .width(32)) STAT_CYCLES (
    .count(MEASURE), .Q(ExecutionCycles), .clk(STAT_CP), .clr(STAT_RESET));  // open: load, D, carry, up
  Counter #(.max('hffffffff), .trigger("falling"), .width(32)) STAT_INSTRUCTIONS (
    .count(and_2_out), .Q(DynamicInstructions), .clk(STAT_CP), .clr(STAT_RESET));  // open: load, D, carry, up
  Counter #(.max('hffffffff), .trigger("falling"), .width(32)) STAT_BRANCHES (
    .count(and_5_out), .Q(DynamicBranchCount), .clk(STAT_CP), .clr(STAT_RESET));  // open: load, D, carry, up
  Counter #(.max('hffffffff), .trigger("falling"), .width(32)) STAT_MEM_READS (
    .count(and_6_out), .Q(MemoryReads), .clk(STAT_CP), .clr(STAT_RESET));  // open: load, D, carry, up
  Counter #(.max('hffffffff), .trigger("falling"), .width(32)) STAT_MEM_WRITES (
    .count(and_4_out), .Q(MemoryWrites), .clk(STAT_CP), .clr(STAT_RESET));  // open: load, D, carry, up

  // Other names for the same wires on the sheet: STAT_MEASURE = MEASURE

  // Notes on the sheet:
  //   BENCHMARK STATISTICS
  //   Set MEASURE=1, pulse STAT_RESET=1 then 0, then run the benchmark.
  //   Counters use the gated processor clock (the same clock net that drives the Mano registers).
  //   Data-memory reads exclude instruction fetches (READ AND NOT IRLD).
  //   Branch metric here counts BUN/BSA via PCLD and ISZ via DRINC; interrupts should be disabled.
  //   Derived after the run: CPI = Cycles / Instructions; IPC = Instructions / Cycles.
  //   Total memory accesses = MemoryReads + MemoryWrites.
  //   Static instruction count and machine-code size are measured from the benchmark program, not by hardware counters.
endmodule

module E_Register (
  input  ELD,
  input  ALU_E,
  input  ECMP,
  input  ECLR,
  input  CP,
  output E
);

  wire and_1_out, and_2_out, not_1_out, or_1_out, or_2_out;

  and and_1 (and_1_out, ELD, ALU_E);
  and and_2 (and_2_out, ELD, not_1_out);
  not not_1 (not_1_out, ALU_E);
  or or_1 (or_1_out, and_1_out, ECMP);
  or or_2 (or_2_out, ECMP, and_2_out, ECLR);
  // Master_Slave_Flip_Flop FGO: pin names not known; wires that end beside it: or_1_out, CP, or_2_out, E
endmodule
